# Fritzing sketch SIM800L-Serial (saved by Fritzing 0.9.10b)
circuit board: 8.46667cm x 5.64444cm

parts:
  M1 = sim800L v2 evb
  USBTTL1 = USB TTL Serial Cable

nets:
  N1: M1.pin_2, M1.pin_6, USBTTL1.GND
  N2: M1.pin_3, USBTTL1.RX
  N3: M1.pin_4, USBTTL1.TX
  N4: M1.pin_7, USBTTL1.5V

custom parts:
  sim800L v2 evb: sim800L v2 evb GSM module.
